# Fritzing sketch Connection (saved by Fritzing 0.9.3b)

parts:
  Part1 = Arduino Uno (Rev3)
  Part2 = Adafruit ADXL345 [part_number="Adafruit #1231"]

nets:
  N1: Part1.A4/SDA, Part2.SDA/SDIO
  N2: Part1.A5/SCL, Part2.SCL
  3V3: Part1.3V3, Part2.3.3V
  GND: Part1.GND, Part2.GND

custom parts:
  Adafruit ADXL345: Filling out our accelerometer offerings, we now have the really lovely digital ADXL345 from Analog Devices, a triple-axis accelerometer with digital I2C and SPI interface breakout. We added an on-board 3.3V regulator and logic-level shifting circuitry, making it a perfect choice for interfacing with any 3V or 5V microcontroller such as the Arduino. The sensor has three axes of measurements, X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
